// Logisim project aiALU.circ as structural Verilog
module aiArith (
  input  [7:0] a,
  input  [7:0] b,
  input  AS,
  input  Cin,
  output [7:0] y
);

  _8bit_Adder u_8bit_adder_1 ();  // open: out_18, in_1, in_2, in_3, in_4, in_5, in_6, in_7, in_8, in_9, in_10, in_11, in_12, in_13, in_14, in_15, in_16, in_17, out_19, out_20, out_21, out_22, out_23, out_24, out_25, out_26
endmodule

module HalfAdder (
  input  A,
  input  B,
  output S,
  output C
);

  xor xor_1 (S, A, B);
  and and_1 (C, A, B);
endmodule

module FullAdder (
  input  A,
  input  B,
  input  Cin,
  output Cout,
  output S
);

  wire halfadder_1_c, halfadder_1_s, halfadder_2_c;

  HalfAdder halfadder_1 (.A(A), .B(B), .S(halfadder_1_s), .C(halfadder_1_c));
  HalfAdder halfadder_2 (.A(halfadder_1_s), .B(Cin), .S(S), .C(halfadder_2_c));
  or or_1 (Cout, halfadder_1_c, halfadder_2_c);
endmodule

module _8bit_Adder (
  input  in_1,
  input  in_2,
  input  in_3,
  input  in_4,
  input  in_5,
  input  in_6,
  input  in_7,
  input  in_8,
  input  in_9,
  input  in_10,
  input  in_11,
  input  in_12,
  input  in_13,
  input  in_14,
  input  in_15,
  input  in_16,
  input  in_17,
  output out_18,
  output out_19,
  output out_20,
  output out_21,
  output out_22,
  output out_23,
  output out_24,
  output out_25,
  output out_26
);

  wire fulladder_1_cout, fulladder_2_cout, fulladder_3_cout, fulladder_4_cout, fulladder_5_cout,
       fulladder_6_cout, fulladder_7_cout;

  FullAdder fulladder_1 (.A(in_1), .B(in_2), .Cin(in_17), .Cout(fulladder_1_cout), .S(out_19));
  FullAdder fulladder_2 (.A(in_3), .B(in_4), .Cin(fulladder_1_cout), .Cout(fulladder_2_cout), .S(out_20));
  FullAdder fulladder_3 (.A(in_5), .B(in_6), .Cin(fulladder_2_cout), .Cout(fulladder_3_cout), .S(out_21));
  FullAdder fulladder_4 (.A(in_7), .B(in_8), .Cin(fulladder_3_cout), .Cout(fulladder_4_cout), .S(out_22));
  FullAdder fulladder_5 (.A(in_9), .B(in_10), .Cin(fulladder_4_cout), .Cout(fulladder_5_cout), .S(out_23));
  FullAdder fulladder_6 (.A(in_11), .B(in_12), .Cin(fulladder_5_cout), .Cout(fulladder_6_cout), .S(out_24));
  FullAdder fulladder_7 (.A(in_13), .B(in_14), .Cin(fulladder_6_cout), .Cout(fulladder_7_cout), .S(out_25));
  FullAdder fulladder_8 (.A(in_15), .B(in_16), .Cin(fulladder_7_cout), .Cout(out_18), .S(out_26));
endmodule
